// Digital circuit overture.dig as structural Verilog
module overture (
  input  C_0,
  input  C_1,
  input  C_2,
  input  [7:0] A_0,
  input  [7:0] B_0,
  input  clk,
  output [7:0] O_0
);

  wire and_7_out, and_8_out, and_9_out, and_10_out, and_11_out, and_12_out, and_13_out, and_14_out,
       and_16_out, and_17_out, and_18_out, and_19_out, and_21_out, and_22_out, and_23_out, and_24_out,
       and_67_out, and_68_out, and_69_out, and_70_out, and_71_out, and_72_out, and_73_out, and_74_out,
       and_79_out, and_80_out, and_81_out, and_82_out, and_83_out, and_84_out, and_85_out, and_93_out,
       and_94_out, and_95_out, and_96_out, and_97_out, and_98_out, and_99_out, and_113_out, and_114_out,
       and_115_out, and_116_out, and_117_out, and_118_out, and_119_out, and_120_out, and_121_out,
       and_122_out, and_123_out, and_124_out, and_125_out, and_126_out, and_127_out, and_128_out,
       and_129_out, and_130_out, and_131_out, and_132_out, and_133_out, and_134_out, and_135_out,
       and_136_out, and_137_out, and_138_out, and_139_out, and_140_out, and_141_out, and_142_out,
       and_143_out, and_144_out, and_145_out, and_146_out, and_147_out, and_148_out, and_149_out,
       and_150_out, and_151_out, and_152_out, and_153_out, and_154_out, and_155_out, and_156_out,
       and_157_out, and_158_out, and_159_out, and_160_out, and_161_out, and_162_out, and_163_out,
       and_164_out, and_165_out, and_166_out, and_167_out, and_169_out, and_170_out, and_171_out,
       and_172_out, and_173_out, and_174_out, and_175_out, and_176_out, and_177_out, and_178_out,
       and_179_out, and_180_out, and_181_out, and_182_out, and_183_out, and_184_out, and_185_out,
       and_186_out, and_187_out, and_188_out, and_189_out, and_190_out, and_191_out, and_192_out,
       and_193_out, and_194_out, and_195_out, and_196_out, and_197_out, and_198_out, and_199_out,
       and_200_out, and_201_out, and_202_out, and_203_out, dipswitch_1_out, dipswitch_2_out, dipswitch_3_out,
       dipswitch_4_out, nand_9_out, nand_10_out, nand_11_out, nand_12_out, nand_13_out, nand_14_out,
       nand_15_out, nand_16_out, nand_17_out, nand_18_out, nand_19_out, nand_20_out, nand_21_out,
       nand_22_out, nand_23_out, nand_24_out, nand_26_out, nand_28_out, nand_30_out, nand_32_out,
       nand_33_out, nand_34_out, nand_35_out, nand_36_out, nand_37_out, nand_38_out, nand_39_out,
       nand_40_out, nand_41_out, nand_42_out, nand_43_out, nand_44_out, nand_45_out, nand_46_out,
       nand_47_out, nand_48_out, nand_50_out, nand_52_out, nand_54_out, nand_56_out, nand_57_out,
       nand_58_out, nand_59_out, nand_60_out, nand_61_out, nand_62_out, nand_63_out, nand_64_out, nor_9_out,
       nor_10_out, nor_11_out, nor_12_out, nor_13_out, nor_14_out, nor_15_out, nor_16_out, nor_17_out,
       nor_18_out, nor_19_out, nor_20_out, nor_21_out, nor_22_out, nor_23_out, nor_24_out, nor_25_out,
       nor_26_out, nor_27_out, nor_28_out, nor_29_out, nor_30_out, nor_31_out, nor_32_out, nor_33_out,
       nor_34_out, not_1_out, not_2_out, not_3_out, not_4_out, not_5_out, not_6_out, not_7_out, not_8_out,
       not_9_out, not_10_out, not_11_out, not_12_out, not_13_out, not_14_out, not_15_out, not_16_out,
       not_17_out, not_18_out, not_19_out, not_20_out, not_21_out, not_22_out, not_23_out, not_24_out,
       not_25_out, notconnected_1_out, notconnected_2_out, notconnected_6_out, notconnected_11_out,
       notconnected_15_out, notconnected_16_out, notconnected_17_out, notconnected_18_out, or_8_out,
       or_9_out, or_10_out, or_11_out, or_12_out, or_13_out, or_14_out, or_15_out, or_17_out, or_66_out,
       or_67_out, or_68_out, or_69_out, or_70_out, or_71_out, or_72_out, or_73_out, or_74_out, or_75_out,
       or_76_out, or_77_out, or_78_out, or_79_out, or_80_out, or_81_out, xor_1_out, xor_2_out, xor_3_out,
       xor_4_out, xor_5_out, xor_6_out, xor_7_out, xor_8_out, xor_15_out, xor_16_out, xor_17_out, xor_18_out,
       xor_19_out, xor_20_out, xor_21_out, xor_22_out, xor_41_out, xor_42_out, xor_43_out, xor_44_out,
       xor_45_out, xor_46_out, xor_47_out, xor_48_out, xor_49_out, xor_50_out, xor_51_out, xor_52_out,
       xor_53_out, xor_54_out, xor_55_out, xor_56_out, xor_57_out, xor_58_out, xor_59_out, xor_60_out,
       xor_61_out, xor_62_out, xor_63_out, xor_64_out, xor_65_out, xor_66_out, xor_67_out, xor_68_out,
       xor_69_out, xor_70_out, xor_71_out, xor_72_out;
  wire [7:0] and_20_out, and_60_out, and_61_out, and_62_out, and_63_out, and_64_out, and_88_out, and_104_out,
       and_112_out, nand_8_out, nand_31_out, nor_8_out, notconnected_3_out, notconnected_4_out,
       notconnected_5_out, notconnected_7_out, notconnected_8_out, notconnected_9_out, notconnected_10_out,
       notconnected_12_out, notconnected_13_out, notconnected_14_out, or_16_out, or_54_out, or_55_out,
       or_56_out, or_57_out, or_65_out, xor_28_out, xor_32_out, xor_40_out;

  xor xor_1 (xor_1_out, B_0[7], and_80_out);
  xor xor_2 (xor_2_out, B_0[6], and_80_out);
  xor xor_3 (xor_3_out, B_0[5], and_80_out);
  xor xor_4 (xor_4_out, B_0[4], and_80_out);
  xor xor_5 (xor_5_out, B_0[3], and_80_out);
  xor xor_6 (xor_6_out, B_0[2], and_80_out);
  xor xor_7 (xor_7_out, B_0[1], and_80_out);
  xor xor_8 (xor_8_out, B_0[0], and_80_out);
  and and_1 (and_20_out[0], B_0[0], A_0[0]);
  nand nand_1 (nand_8_out[0], B_0[0], A_0[0]);
  or or_1 (or_16_out[0], B_0[0], A_0[0]);
  nor nor_1 (nor_8_out[0], B_0[0], A_0[0]);
  xor xor_9 (xor_28_out[0], B_0[0], A_0[0]);
  and and_2 (and_20_out[1], B_0[1], A_0[1]);
  nand nand_2 (nand_8_out[1], B_0[1], A_0[1]);
  or or_2 (or_16_out[1], B_0[1], A_0[1]);
  nor nor_2 (nor_8_out[1], B_0[1], A_0[1]);
  xor xor_10 (xor_28_out[1], B_0[1], A_0[1]);
  and and_3 (and_20_out[2], B_0[2], A_0[2]);
  nand nand_3 (nand_8_out[2], B_0[2], A_0[2]);
  or or_3 (or_16_out[2], B_0[2], A_0[2]);
  nor nor_3 (nor_8_out[2], B_0[2], A_0[2]);
  xor xor_11 (xor_28_out[2], B_0[2], A_0[2]);
  and and_4 (and_20_out[3], B_0[3], A_0[3]);
  and and_5 (and_20_out[4], B_0[4], A_0[4]);
  nand nand_4 (nand_8_out[3], B_0[3], A_0[3]);
  nand nand_5 (nand_8_out[4], B_0[4], A_0[4]);
  or or_4 (or_16_out[3], B_0[3], A_0[3]);
  or or_5 (or_16_out[4], B_0[4], A_0[4]);
  nor nor_4 (nor_8_out[3], B_0[3], A_0[3]);
  nor nor_5 (nor_8_out[4], B_0[4], A_0[4]);
  xor xor_12 (xor_28_out[3], B_0[3], A_0[3]);
  xor xor_13 (xor_28_out[4], B_0[4], A_0[4]);
  and and_6 (and_20_out[5], B_0[5], A_0[5]);
  nand nand_6 (nand_8_out[5], B_0[5], A_0[5]);
  or or_6 (or_16_out[5], B_0[5], A_0[5]);
  nor nor_6 (nor_8_out[5], B_0[5], A_0[5]);
  xor xor_14 (xor_28_out[5], B_0[5], A_0[5]);
  and and_7 (and_7_out, xor_1_out, A_0[7]);
  xor xor_15 (xor_15_out, A_0[7], xor_1_out);
  and and_8 (and_8_out, xor_2_out, A_0[6]);
  xor xor_16 (xor_16_out, A_0[6], xor_2_out);
  and and_9 (and_9_out, xor_3_out, A_0[5]);
  xor xor_17 (xor_17_out, A_0[5], xor_3_out);
  and and_10 (and_10_out, xor_4_out, A_0[4]);
  xor xor_18 (xor_18_out, A_0[4], xor_4_out);
  and and_11 (and_11_out, xor_5_out, A_0[3]);
  xor xor_19 (xor_19_out, A_0[3], xor_5_out);
  and and_12 (and_12_out, xor_6_out, A_0[2]);
  xor xor_20 (xor_20_out, A_0[2], xor_6_out);
  and and_13 (and_13_out, xor_7_out, A_0[1]);
  xor xor_21 (xor_21_out, A_0[1], xor_7_out);
  and and_14 (and_14_out, xor_8_out, A_0[0]);
  xor xor_22 (xor_22_out, A_0[0], xor_8_out);
  and and_15 (and_20_out[6], B_0[6], A_0[6]);
  nand nand_7 (nand_8_out[6], B_0[6], A_0[6]);
  or or_7 (or_16_out[6], B_0[6], A_0[6]);
  nor nor_7 (nor_8_out[6], B_0[6], A_0[6]);
  xor xor_23 (xor_28_out[6], B_0[6], A_0[6]);
  or or_8 (or_8_out, and_7_out, and_16_out);
  and and_16 (and_16_out, xor_15_out, or_9_out);
  xor xor_24 (xor_32_out[7], xor_15_out, or_9_out);
  or or_9 (or_9_out, and_8_out, and_17_out);
  and and_17 (and_17_out, xor_16_out, or_10_out);
  xor xor_25 (xor_32_out[6], xor_16_out, or_10_out);
  or or_10 (or_10_out, and_9_out, and_18_out);
  and and_18 (and_18_out, xor_17_out, or_11_out);
  xor xor_26 (xor_32_out[5], xor_17_out, or_11_out);
  or or_11 (or_11_out, and_10_out, and_19_out);
  and and_19 (and_19_out, xor_18_out, or_12_out);
  xor xor_27 (xor_32_out[4], xor_18_out, or_12_out);
  or or_12 (or_12_out, and_11_out, and_21_out);
  or or_13 (or_13_out, and_12_out, and_22_out);
  or or_14 (or_14_out, and_13_out, and_23_out);
  or or_15 (or_15_out, and_14_out, and_24_out);
  and and_20 (and_20_out[7], B_0[7], A_0[7]);
  nand nand_8 (nand_8_out[7], B_0[7], A_0[7]);
  or or_16 (or_16_out[7], B_0[7], A_0[7]);
  nor nor_8 (nor_8_out[7], B_0[7], A_0[7]);
  xor xor_28 (xor_28_out[7], B_0[7], A_0[7]);
  and and_21 (and_21_out, xor_19_out, or_13_out);
  xor xor_29 (xor_32_out[3], xor_19_out, or_13_out);
  and and_22 (and_22_out, xor_20_out, or_14_out);
  xor xor_30 (xor_32_out[2], xor_20_out, or_14_out);
  and and_23 (and_23_out, xor_21_out, or_15_out);
  xor xor_31 (xor_32_out[1], xor_21_out, or_15_out);
  and and_24 (and_24_out, xor_22_out, and_80_out);
  xor xor_32 (xor_32_out[0], xor_22_out, and_80_out);
  and and_25 (and_60_out[0], and_81_out, and_20_out[0]);
  and and_26 (and_60_out[1], and_81_out, and_20_out[1]);
  and and_27 (and_61_out[0], and_82_out, nand_8_out[0]);
  and and_28 (and_61_out[1], and_82_out, nand_8_out[1]);
  and and_29 (and_62_out[0], and_83_out, or_16_out[0]);
  and and_30 (and_62_out[1], and_83_out, or_16_out[1]);
  and and_31 (and_63_out[0], and_84_out, nor_8_out[0]);
  and and_32 (and_63_out[1], and_84_out, nor_8_out[1]);
  and and_33 (and_64_out[0], and_85_out, xor_28_out[0]);
  and and_34 (and_64_out[1], and_85_out, xor_28_out[1]);
  and and_35 (and_60_out[2], and_81_out, and_20_out[2]);
  and and_36 (and_61_out[2], and_82_out, nand_8_out[2]);
  and and_37 (and_62_out[2], and_83_out, or_16_out[2]);
  and and_38 (and_63_out[2], and_84_out, nor_8_out[2]);
  and and_39 (and_64_out[2], and_85_out, xor_28_out[2]);
  and and_40 (and_60_out[3], and_81_out, and_20_out[3]);
  and and_41 (and_61_out[3], and_82_out, nand_8_out[3]);
  and and_42 (and_62_out[3], and_83_out, or_16_out[3]);
  and and_43 (and_63_out[3], and_84_out, nor_8_out[3]);
  and and_44 (and_64_out[3], and_85_out, xor_28_out[3]);
  and and_45 (and_60_out[4], and_81_out, and_20_out[4]);
  and and_46 (and_60_out[5], and_81_out, and_20_out[5]);
  and and_47 (and_61_out[4], and_82_out, nand_8_out[4]);
  and and_48 (and_61_out[5], and_82_out, nand_8_out[5]);
  and and_49 (and_62_out[4], and_83_out, or_16_out[4]);
  and and_50 (and_62_out[5], and_83_out, or_16_out[5]);
  and and_51 (and_63_out[4], and_84_out, nor_8_out[4]);
  and and_52 (and_63_out[5], and_84_out, nor_8_out[5]);
  and and_53 (and_64_out[4], and_85_out, xor_28_out[4]);
  and and_54 (and_64_out[5], and_85_out, xor_28_out[5]);
  and and_55 (and_60_out[6], and_81_out, and_20_out[6]);
  and and_56 (and_61_out[6], and_82_out, nand_8_out[6]);
  and and_57 (and_62_out[6], and_83_out, or_16_out[6]);
  and and_58 (and_63_out[6], and_84_out, nor_8_out[6]);
  and and_59 (and_64_out[6], and_85_out, xor_28_out[6]);
  and and_60 (and_60_out[7], and_81_out, and_20_out[7]);
  and and_61 (and_61_out[7], and_82_out, nand_8_out[7]);
  and and_62 (and_62_out[7], and_83_out, or_16_out[7]);
  and and_63 (and_63_out[7], and_84_out, nor_8_out[7]);
  and and_64 (and_64_out[7], and_85_out, xor_28_out[7]);
  not not_1 (not_1_out, C_2);
  and and_65 (and_88_out[0], or_17_out, xor_32_out[0]);
  not not_2 (not_2_out, C_1);
  not not_3 (not_3_out, C_1);
  and and_66 (and_88_out[1], or_17_out, xor_32_out[1]);
  not not_4 (not_4_out, C_0);
  and and_67 (and_67_out, not_4_out, not_2_out);
  and and_68 (and_68_out, C_0, not_2_out);
  and and_69 (and_69_out, not_4_out, C_1);
  and and_70 (and_70_out, C_1, C_0);
  not not_5 (not_5_out, C_2);
  not not_6 (not_6_out, C_0);
  and and_71 (and_71_out, not_6_out, not_3_out);
  and and_72 (and_72_out, C_0, not_3_out);
  and and_73 (and_73_out, not_6_out, C_1);
  and and_74 (and_74_out, C_1, C_0);
  not not_7 (not_7_out, not_1_out);
  and and_75 (and_88_out[2], or_17_out, xor_32_out[2]);
  and and_76 (and_88_out[3], or_17_out, xor_32_out[3]);
  and and_77 (and_88_out[4], or_17_out, xor_32_out[4]);
  // And and_78 has open pins: In_1=and_67_out, In_2=not_5_out, out=open
  and and_79 (and_79_out, and_68_out, not_5_out);
  and and_80 (and_80_out, and_69_out, not_5_out);
  and and_81 (and_81_out, and_70_out, not_5_out);
  and and_82 (and_82_out, and_71_out, not_7_out);
  and and_83 (and_83_out, and_72_out, not_7_out);
  and and_84 (and_84_out, and_73_out, not_7_out);
  and and_85 (and_85_out, and_74_out, not_7_out);
  and and_86 (and_88_out[5], or_17_out, xor_32_out[5]);
  and and_87 (and_88_out[6], or_17_out, xor_32_out[6]);
  and and_88 (and_88_out[7], or_17_out, xor_32_out[7]);
  or or_17 (or_17_out, and_79_out, and_80_out);
  or or_18 (O_0[0], and_88_out[0], or_54_out[0]);
  or or_19 (or_54_out[0], and_60_out[0], or_55_out[0]);
  or or_20 (or_55_out[0], and_61_out[0], or_56_out[0]);
  or or_21 (or_56_out[0], and_62_out[0], or_57_out[0]);
  or or_22 (or_57_out[0], and_63_out[0], and_64_out[0]);
  or or_23 (O_0[1], and_88_out[1], or_54_out[1]);
  or or_24 (or_54_out[1], and_60_out[1], or_55_out[1]);
  or or_25 (or_55_out[1], and_61_out[1], or_56_out[1]);
  or or_26 (or_56_out[1], and_62_out[1], or_57_out[1]);
  or or_27 (or_57_out[1], and_63_out[1], and_64_out[1]);
  or or_28 (O_0[2], and_88_out[2], or_54_out[2]);
  or or_29 (or_54_out[2], and_60_out[2], or_55_out[2]);
  or or_30 (or_55_out[2], and_61_out[2], or_56_out[2]);
  or or_31 (or_56_out[2], and_62_out[2], or_57_out[2]);
  or or_32 (or_57_out[2], and_63_out[2], and_64_out[2]);
  or or_33 (O_0[3], and_88_out[3], or_54_out[3]);
  or or_34 (O_0[4], and_88_out[4], or_54_out[4]);
  or or_35 (or_54_out[3], and_60_out[3], or_55_out[3]);
  or or_36 (or_54_out[4], and_60_out[4], or_55_out[4]);
  or or_37 (or_55_out[3], and_61_out[3], or_56_out[3]);
  or or_38 (or_55_out[4], and_61_out[4], or_56_out[4]);
  or or_39 (or_56_out[3], and_62_out[3], or_57_out[3]);
  or or_40 (or_56_out[4], and_62_out[4], or_57_out[4]);
  or or_41 (or_57_out[3], and_63_out[3], and_64_out[3]);
  or or_42 (or_57_out[4], and_63_out[4], and_64_out[4]);
  or or_43 (O_0[5], and_88_out[5], or_54_out[5]);
  or or_44 (or_54_out[5], and_60_out[5], or_55_out[5]);
  or or_45 (or_55_out[5], and_61_out[5], or_56_out[5]);
  or or_46 (or_56_out[5], and_62_out[5], or_57_out[5]);
  or or_47 (or_57_out[5], and_63_out[5], and_64_out[5]);
  or or_48 (O_0[6], and_88_out[6], or_54_out[6]);
  or or_49 (or_54_out[6], and_60_out[6], or_55_out[6]);
  or or_50 (or_55_out[6], and_61_out[6], or_56_out[6]);
  or or_51 (or_56_out[6], and_62_out[6], or_57_out[6]);
  or or_52 (or_57_out[6], and_63_out[6], and_64_out[6]);
  or or_53 (O_0[7], and_88_out[7], or_54_out[7]);
  or or_54 (or_54_out[7], and_60_out[7], or_55_out[7]);
  or or_55 (or_55_out[7], and_61_out[7], or_56_out[7]);
  or or_56 (or_56_out[7], and_62_out[7], or_57_out[7]);
  or or_57 (or_57_out[7], and_63_out[7], and_64_out[7]);
  DipSwitch dipswitch_1 (.out(dipswitch_1_out));
  and and_89 (and_104_out[0], dipswitch_1_out, 1'b0);
  and and_90 (and_104_out[1], dipswitch_1_out, 1'b0);
  and and_91 (and_104_out[2], dipswitch_1_out, 1'b0);
  // And and_92 has open pins: In_1=and_93_out, In_2=nand_31_out[7], out=open
  xor xor_33 (xor_40_out[7], nand_31_out[7], and_93_out);
  and and_93 (and_93_out, and_94_out, nand_31_out[6]);
  xor xor_34 (xor_40_out[6], nand_31_out[6], and_94_out);
  and and_94 (and_94_out, and_95_out, nand_31_out[5]);
  xor xor_35 (xor_40_out[5], nand_31_out[5], and_95_out);
  and and_95 (and_95_out, and_96_out, nand_31_out[4]);
  xor xor_36 (xor_40_out[4], nand_31_out[4], and_96_out);
  and and_96 (and_96_out, and_97_out, nand_31_out[3]);
  xor xor_37 (xor_40_out[3], nand_31_out[3], and_97_out);
  and and_97 (and_97_out, and_98_out, nand_31_out[2]);
  xor xor_38 (xor_40_out[2], nand_31_out[2], and_98_out);
  and and_98 (and_98_out, and_99_out, nand_31_out[1]);
  xor xor_39 (xor_40_out[1], nand_31_out[1], and_99_out);
  and and_99 (and_99_out, 1'b1, nand_31_out[0]);
  xor xor_40 (xor_40_out[0], nand_31_out[0], 1'b1);
  and and_100 (and_104_out[3], dipswitch_1_out, 1'b0);
  and and_101 (and_104_out[4], dipswitch_1_out, 1'b0);
  and and_102 (and_104_out[5], dipswitch_1_out, 1'b0);
  and and_103 (and_104_out[6], dipswitch_1_out, 1'b0);
  not not_8 (not_8_out, dipswitch_1_out);
  and and_104 (and_104_out[7], dipswitch_1_out, 1'b0);
  or or_58 (or_65_out[0], and_112_out[0], and_104_out[0]);
  or or_59 (or_65_out[1], and_112_out[1], and_104_out[1]);
  or or_60 (or_65_out[2], and_112_out[2], and_104_out[2]);
  and and_105 (and_112_out[0], not_8_out, xor_40_out[0]);
  and and_106 (and_112_out[1], not_8_out, xor_40_out[1]);
  and and_107 (and_112_out[2], not_8_out, xor_40_out[2]);
  and and_108 (and_112_out[3], not_8_out, xor_40_out[3]);
  and and_109 (and_112_out[4], not_8_out, xor_40_out[4]);
  and and_110 (and_112_out[5], not_8_out, xor_40_out[5]);
  and and_111 (and_112_out[6], not_8_out, xor_40_out[6]);
  and and_112 (and_112_out[7], not_8_out, xor_40_out[7]);
  or or_61 (or_65_out[3], and_112_out[3], and_104_out[3]);
  or or_62 (or_65_out[4], and_112_out[4], and_104_out[4]);
  or or_63 (or_65_out[5], and_112_out[5], and_104_out[5]);
  or or_64 (or_65_out[6], and_112_out[6], and_104_out[6]);
  or or_65 (or_65_out[7], and_112_out[7], and_104_out[7]);
  // NotConnected on notconnected_1_out
  // NotConnected on notconnected_2_out
  // NotConnected on notconnected_3_out
  // NotConnected on notconnected_4_out
  // NotConnected on notconnected_5_out
  nand nand_9 (nand_9_out, nand_12_out, nand_10_out);
  nand nand_10 (nand_10_out, nand_9_out, clk);
  nand nand_11 (nand_11_out, nand_10_out, clk, nand_12_out);
  nand nand_12 (nand_12_out, nand_11_out, or_65_out[6]);
  nand nand_13 (nand_13_out, nand_16_out, nand_14_out);
  nand nand_14 (nand_14_out, nand_13_out, clk);
  nand nand_15 (nand_15_out, nand_14_out, clk, nand_16_out);
  nand nand_16 (nand_16_out, nand_15_out, or_65_out[4]);
  nand nand_17 (nand_17_out, nand_20_out, nand_18_out);
  nand nand_18 (nand_18_out, nand_17_out, clk);
  nand nand_19 (nand_19_out, nand_18_out, clk, nand_20_out);
  nand nand_20 (nand_20_out, nand_19_out, or_65_out[2]);
  nand nand_21 (nand_21_out, nand_24_out, nand_22_out);
  nand nand_22 (nand_22_out, nand_21_out, clk);
  nand nand_23 (nand_23_out, nand_22_out, clk, nand_24_out);
  nand nand_24 (nand_24_out, nand_23_out, or_65_out[0]);
  nand nand_25 (nand_31_out[6], nand_10_out, nand_26_out);
  nand nand_26 (nand_26_out, nand_31_out[6], nand_11_out);
  nand nand_27 (nand_31_out[4], nand_14_out, nand_28_out);
  nand nand_28 (nand_28_out, nand_31_out[4], nand_15_out);
  nand nand_29 (nand_31_out[2], nand_18_out, nand_30_out);
  nand nand_30 (nand_30_out, nand_31_out[2], nand_19_out);
  nand nand_31 (nand_31_out[0], nand_22_out, nand_32_out);
  nand nand_32 (nand_32_out, nand_31_out[0], nand_23_out);
  DipSwitch dipswitch_2 (.out(dipswitch_2_out));
  DipSwitch dipswitch_3 (.out(dipswitch_3_out));
  DipSwitch dipswitch_4 (.out(dipswitch_4_out));
  not not_9 (not_9_out, notconnected_3_out[7]);
  and and_113 (and_113_out, notconnected_1_out, notconnected_3_out[7]);
  not not_10 (not_10_out, notconnected_3_out[6]);
  and and_114 (and_114_out, notconnected_1_out, notconnected_3_out[6]);
  not not_11 (not_11_out, notconnected_3_out[5]);
  and and_115 (and_115_out, notconnected_1_out, notconnected_3_out[5]);
  not not_12 (not_12_out, notconnected_3_out[4]);
  and and_116 (and_116_out, notconnected_1_out, notconnected_3_out[4]);
  not not_13 (not_13_out, notconnected_3_out[3]);
  and and_117 (and_117_out, notconnected_1_out, notconnected_3_out[3]);
  not not_14 (not_14_out, notconnected_3_out[2]);
  and and_118 (and_118_out, notconnected_1_out, notconnected_3_out[2]);
  not not_15 (not_15_out, notconnected_3_out[1]);
  and and_119 (and_119_out, notconnected_1_out, notconnected_3_out[1]);
  not not_16 (not_16_out, notconnected_3_out[0]);
  and and_120 (and_120_out, notconnected_1_out, notconnected_3_out[0]);
  and and_121 (and_121_out, nand_31_out[6], 1'b0);
  and and_122 (and_122_out, nand_31_out[4], 1'b0);
  and and_123 (and_123_out, nand_31_out[2], 1'b0);
  and and_124 (and_124_out, nand_31_out[0], 1'b0);
  and and_125 (and_125_out, not_17_out, dipswitch_3_out);
  not not_17 (not_17_out, dipswitch_4_out);
  and and_126 (and_126_out, dipswitch_3_out, dipswitch_4_out);
  and and_127 (and_127_out, not_9_out, notconnected_1_out);
  and and_128 (and_128_out, not_10_out, notconnected_1_out);
  and and_129 (and_129_out, not_11_out, notconnected_1_out);
  and and_130 (and_130_out, not_12_out, notconnected_1_out);
  and and_131 (and_131_out, not_13_out, notconnected_1_out);
  and and_132 (and_132_out, not_14_out, notconnected_1_out);
  and and_133 (and_133_out, not_15_out, notconnected_1_out);
  and and_134 (and_134_out, not_16_out, notconnected_1_out);
  nor nor_9 (nor_9_out, and_127_out, nor_10_out);
  nor nor_10 (nor_10_out, nor_9_out, and_113_out);
  nor nor_11 (nor_11_out, and_128_out, nor_12_out);
  nor nor_12 (nor_12_out, nor_11_out, and_114_out);
  nor nor_13 (nor_13_out, and_129_out, nor_14_out);
  nor nor_14 (nor_14_out, nor_13_out, and_115_out);
  nor nor_15 (nor_15_out, and_130_out, nor_16_out);
  nor nor_16 (nor_16_out, nor_15_out, and_116_out);
  nor nor_17 (nor_17_out, and_131_out, nor_18_out);
  nor nor_18 (nor_18_out, nor_17_out, and_117_out);
  nor nor_19 (nor_19_out, and_132_out, nor_20_out);
  nor nor_20 (nor_20_out, nor_19_out, and_118_out);
  nor nor_21 (nor_21_out, and_133_out, nor_22_out);
  nor nor_22 (nor_22_out, nor_21_out, and_119_out);
  nor nor_23 (nor_23_out, and_134_out, nor_24_out);
  nor nor_24 (nor_24_out, nor_23_out, and_120_out);
  and and_135 (and_135_out, notconnected_4_out[7], notconnected_5_out[7]);
  xor xor_41 (xor_41_out, notconnected_5_out[7], notconnected_4_out[7]);
  and and_136 (and_136_out, notconnected_4_out[6], notconnected_5_out[6]);
  xor xor_42 (xor_42_out, notconnected_5_out[6], notconnected_4_out[6]);
  and and_137 (and_137_out, notconnected_4_out[5], notconnected_5_out[5]);
  xor xor_43 (xor_43_out, notconnected_5_out[5], notconnected_4_out[5]);
  and and_138 (and_138_out, notconnected_4_out[4], notconnected_5_out[4]);
  xor xor_44 (xor_44_out, notconnected_5_out[4], notconnected_4_out[4]);
  and and_139 (and_139_out, notconnected_4_out[3], notconnected_5_out[3]);
  xor xor_45 (xor_45_out, notconnected_5_out[3], notconnected_4_out[3]);
  and and_140 (and_140_out, notconnected_4_out[2], notconnected_5_out[2]);
  xor xor_46 (xor_46_out, notconnected_5_out[2], notconnected_4_out[2]);
  and and_141 (and_141_out, notconnected_4_out[1], notconnected_5_out[1]);
  xor xor_47 (xor_47_out, notconnected_5_out[1], notconnected_4_out[1]);
  and and_142 (and_142_out, notconnected_4_out[0], notconnected_5_out[0]);
  xor xor_48 (xor_48_out, notconnected_5_out[0], notconnected_4_out[0]);
  nor nor_25 (nor_25_out, and_125_out, nor_26_out);
  nor nor_26 (nor_26_out, nor_25_out, and_126_out);
  or or_66 (or_66_out, and_135_out, and_143_out);
  and and_143 (and_143_out, xor_41_out, or_67_out);
  xor xor_49 (xor_49_out, xor_41_out, or_67_out);
  or or_67 (or_67_out, and_136_out, and_144_out);
  and and_144 (and_144_out, xor_42_out, or_68_out);
  xor xor_50 (xor_50_out, xor_42_out, or_68_out);
  or or_68 (or_68_out, and_137_out, and_145_out);
  and and_145 (and_145_out, xor_43_out, or_69_out);
  xor xor_51 (xor_51_out, xor_43_out, or_69_out);
  or or_69 (or_69_out, and_138_out, and_146_out);
  and and_146 (and_146_out, xor_44_out, or_70_out);
  xor xor_52 (xor_52_out, xor_44_out, or_70_out);
  or or_70 (or_70_out, and_139_out, and_155_out);
  or or_71 (or_71_out, and_140_out, and_156_out);
  or or_72 (or_72_out, and_141_out, and_157_out);
  or or_73 (or_73_out, and_142_out, and_158_out);
  // NotConnected on notconnected_6_out
  Reset reset_1 ();  // open: out
  Reset reset_2 ();  // open: out
  and and_147 (and_147_out, nor_9_out, notconnected_2_out);
  Reset reset_3 ();  // open: out
  and and_148 (and_148_out, nor_11_out, notconnected_2_out);
  Reset reset_4 ();  // open: out
  and and_149 (and_149_out, nor_13_out, notconnected_2_out);
  Reset reset_5 ();  // open: out
  and and_150 (and_150_out, nor_15_out, notconnected_2_out);
  Reset reset_6 ();  // open: out
  and and_151 (and_151_out, nor_17_out, notconnected_2_out);
  Reset reset_7 ();  // open: out
  and and_152 (and_152_out, nor_19_out, notconnected_2_out);
  Reset reset_8 ();  // open: out
  and and_153 (and_153_out, nor_21_out, notconnected_2_out);
  Reset reset_9 ();  // open: out
  and and_154 (and_154_out, nor_23_out, notconnected_2_out);
  nand nand_33 (nand_33_out, nand_36_out, nand_34_out);
  nand nand_34 (nand_34_out, nand_33_out, clk);
  nand nand_35 (nand_35_out, nand_34_out, clk, nand_36_out);
  nand nand_36 (nand_36_out, nand_35_out, or_65_out[7]);
  nand nand_37 (nand_37_out, nand_40_out, nand_38_out);
  nand nand_38 (nand_38_out, nand_37_out, clk);
  nand nand_39 (nand_39_out, nand_38_out, clk, nand_40_out);
  nand nand_40 (nand_40_out, nand_39_out, or_65_out[5]);
  nand nand_41 (nand_41_out, nand_44_out, nand_42_out);
  nand nand_42 (nand_42_out, nand_41_out, clk);
  nand nand_43 (nand_43_out, nand_42_out, clk, nand_44_out);
  nand nand_44 (nand_44_out, nand_43_out, or_65_out[3]);
  nand nand_45 (nand_45_out, nand_48_out, nand_46_out);
  nand nand_46 (nand_46_out, nand_45_out, clk);
  nand nand_47 (nand_47_out, nand_46_out, clk, nand_48_out);
  nand nand_48 (nand_48_out, nand_47_out, or_65_out[1]);
  and and_155 (and_155_out, xor_45_out, or_71_out);
  xor xor_53 (xor_53_out, xor_45_out, or_71_out);
  and and_156 (and_156_out, xor_46_out, or_72_out);
  xor xor_54 (xor_54_out, xor_46_out, or_72_out);
  and and_157 (and_157_out, xor_47_out, or_73_out);
  xor xor_55 (xor_55_out, xor_47_out, or_73_out);
  and and_158 (and_158_out, xor_48_out, notconnected_6_out);
  xor xor_56 (xor_56_out, xor_48_out, notconnected_6_out);
  and and_159 (and_159_out, nor_25_out, dipswitch_2_out);
  nand nand_49 (nand_31_out[7], nand_34_out, nand_50_out);
  nand nand_50 (nand_50_out, nand_31_out[7], nand_35_out);
  and and_160 (and_160_out, nand_31_out[7], 1'b0);
  nand nand_51 (nand_31_out[5], nand_38_out, nand_52_out);
  nand nand_52 (nand_52_out, nand_31_out[5], nand_39_out);
  and and_161 (and_161_out, nand_31_out[5], 1'b0);
  nand nand_53 (nand_31_out[3], nand_42_out, nand_54_out);
  nand nand_54 (nand_54_out, nand_31_out[3], nand_43_out);
  and and_162 (and_162_out, nand_31_out[3], 1'b0);
  nand nand_55 (nand_31_out[1], nand_46_out, nand_56_out);
  nand nand_56 (nand_56_out, nand_31_out[1], nand_47_out);
  and and_163 (and_163_out, nand_31_out[1], 1'b0);
  // NotConnected on notconnected_7_out
  // NotConnected on notconnected_8_out
  // NotConnected on notconnected_9_out
  // NotConnected on notconnected_10_out
  and and_164 (and_164_out, notconnected_8_out[0], notconnected_8_out[0]);
  or or_74 (or_74_out, notconnected_9_out[0], notconnected_9_out[0]);
  xor xor_57 (xor_57_out, notconnected_10_out[0], notconnected_10_out[0]);
  and and_165 (and_165_out, notconnected_8_out[1], notconnected_8_out[1]);
  or or_75 (or_75_out, notconnected_9_out[1], notconnected_9_out[1]);
  xor xor_58 (xor_58_out, notconnected_10_out[1], notconnected_10_out[1]);
  not not_18 (not_18_out, notconnected_11_out);
  // NotConnected on notconnected_11_out
  and and_166 (and_166_out, notconnected_8_out[2], notconnected_8_out[2]);
  and and_167 (and_167_out, notconnected_8_out[3], notconnected_8_out[3]);
  or or_76 (or_76_out, notconnected_9_out[2], notconnected_9_out[2]);
  or or_77 (or_77_out, notconnected_9_out[3], notconnected_9_out[3]);
  xor xor_59 (xor_59_out, notconnected_10_out[2], notconnected_10_out[2]);
  xor xor_60 (xor_60_out, notconnected_10_out[3], notconnected_10_out[3]);
  // And and_168 has open pins: In_1=and_169_out, In_2=notconnected_7_out[7], out=open
  xor xor_61 (xor_61_out, notconnected_7_out[7], and_169_out);
  and and_169 (and_169_out, and_170_out, notconnected_7_out[6]);
  xor xor_62 (xor_62_out, notconnected_7_out[6], and_170_out);
  and and_170 (and_170_out, and_171_out, notconnected_7_out[5]);
  xor xor_63 (xor_63_out, notconnected_7_out[5], and_171_out);
  and and_171 (and_171_out, and_172_out, notconnected_7_out[4]);
  xor xor_64 (xor_64_out, notconnected_7_out[4], and_172_out);
  and and_172 (and_172_out, and_173_out, notconnected_7_out[3]);
  xor xor_65 (xor_65_out, notconnected_7_out[3], and_173_out);
  and and_173 (and_173_out, and_174_out, notconnected_7_out[2]);
  xor xor_66 (xor_66_out, notconnected_7_out[2], and_174_out);
  and and_174 (and_174_out, and_175_out, notconnected_7_out[1]);
  xor xor_67 (xor_67_out, notconnected_7_out[1], and_175_out);
  and and_175 (and_175_out, not_18_out, notconnected_7_out[0]);
  xor xor_68 (xor_68_out, notconnected_7_out[0], not_18_out);
  and and_176 (and_176_out, notconnected_8_out[4], notconnected_8_out[4]);
  or or_78 (or_78_out, notconnected_9_out[4], notconnected_9_out[4]);
  xor xor_69 (xor_69_out, notconnected_10_out[4], notconnected_10_out[4]);
  and and_177 (and_177_out, notconnected_8_out[5], notconnected_8_out[5]);
  or or_79 (or_79_out, notconnected_9_out[5], notconnected_9_out[5]);
  xor xor_70 (xor_70_out, notconnected_10_out[5], notconnected_10_out[5]);
  and and_178 (and_178_out, notconnected_8_out[6], notconnected_8_out[6]);
  and and_179 (and_179_out, notconnected_8_out[7], notconnected_8_out[7]);
  or or_80 (or_80_out, notconnected_9_out[6], notconnected_9_out[6]);
  or or_81 (or_81_out, notconnected_9_out[7], notconnected_9_out[7]);
  xor xor_71 (xor_71_out, notconnected_10_out[6], notconnected_10_out[6]);
  xor xor_72 (xor_72_out, notconnected_10_out[7], notconnected_10_out[7]);
  // NotConnected on notconnected_12_out
  // NotConnected on notconnected_13_out
  // NotConnected on notconnected_14_out
  // NotConnected on notconnected_15_out
  // NotConnected on notconnected_16_out
  // NotConnected on notconnected_17_out
  and and_180 (and_180_out, notconnected_18_out, notconnected_12_out[0]);
  nand nand_57 (nand_57_out, notconnected_13_out[0], notconnected_13_out[0]);
  nor nor_27 (nor_27_out, notconnected_14_out[0], notconnected_14_out[0]);
  not not_19 (not_19_out, notconnected_17_out);
  and and_181 (and_181_out, notconnected_18_out, notconnected_12_out[1]);
  and and_182 (and_182_out, notconnected_18_out, notconnected_12_out[2]);
  nand nand_58 (nand_58_out, notconnected_13_out[1], notconnected_13_out[1]);
  nand nand_59 (nand_59_out, notconnected_13_out[2], notconnected_13_out[2]);
  nor nor_28 (nor_28_out, notconnected_14_out[1], notconnected_14_out[1]);
  nor nor_29 (nor_29_out, notconnected_14_out[2], notconnected_14_out[2]);
  not not_20 (not_20_out, notconnected_16_out);
  not not_21 (not_21_out, notconnected_15_out);
  not not_22 (not_22_out, notconnected_17_out);
  not not_23 (not_23_out, notconnected_16_out);
  not not_24 (not_24_out, notconnected_15_out);
  not not_25 (not_25_out, not_19_out);
  // NotConnected on notconnected_18_out
  and and_183 (and_183_out, notconnected_18_out, notconnected_12_out[3]);
  nand nand_60 (nand_60_out, notconnected_13_out[3], notconnected_13_out[3]);
  nor nor_30 (nor_30_out, notconnected_14_out[3], notconnected_14_out[3]);
  and and_184 (and_184_out, not_21_out, not_20_out);
  and and_185 (and_185_out, notconnected_15_out, not_20_out);
  and and_186 (and_186_out, not_21_out, notconnected_16_out);
  and and_187 (and_187_out, notconnected_16_out, notconnected_15_out);
  and and_188 (and_188_out, not_24_out, not_23_out);
  and and_189 (and_189_out, notconnected_15_out, not_23_out);
  and and_190 (and_190_out, not_24_out, notconnected_16_out);
  and and_191 (and_191_out, notconnected_16_out, notconnected_15_out);
  and and_192 (and_192_out, notconnected_18_out, notconnected_12_out[4]);
  nand nand_61 (nand_61_out, notconnected_13_out[4], notconnected_13_out[4]);
  nor nor_31 (nor_31_out, notconnected_14_out[4], notconnected_14_out[4]);
  and and_193 (and_193_out, and_184_out, not_22_out);
  and and_194 (and_194_out, and_185_out, not_22_out);
  and and_195 (and_195_out, and_186_out, not_22_out);
  and and_196 (and_196_out, and_187_out, not_22_out);
  and and_197 (and_197_out, and_188_out, not_25_out);
  and and_198 (and_198_out, and_189_out, not_25_out);
  and and_199 (and_199_out, and_190_out, not_25_out);
  and and_200 (and_200_out, and_191_out, not_25_out);
  and and_201 (and_201_out, notconnected_18_out, notconnected_12_out[5]);
  and and_202 (and_202_out, notconnected_18_out, notconnected_12_out[6]);
  nand nand_62 (nand_62_out, notconnected_13_out[5], notconnected_13_out[5]);
  nand nand_63 (nand_63_out, notconnected_13_out[6], notconnected_13_out[6]);
  nor nor_32 (nor_32_out, notconnected_14_out[5], notconnected_14_out[5]);
  nor nor_33 (nor_33_out, notconnected_14_out[6], notconnected_14_out[6]);
  and and_203 (and_203_out, notconnected_18_out, notconnected_12_out[7]);
  nand nand_64 (nand_64_out, notconnected_13_out[7], notconnected_13_out[7]);
  nor nor_34 (nor_34_out, notconnected_14_out[7], notconnected_14_out[7]);

  // Notes on the sheet:
  //   B
  //   A
  //   ALU
  //   ADDER
  //   AND
  //   NAND
  //   OR
  //   NOR
  //   XOR
  //   .
  //   SWITCH
  //   3x8 Demux
  //   A1
  //   A2
  //   A3
  //   2x4 Demux
  //   A_0
  //   A_1
  //   Disable
  //   Overwrite Value
  //   Overwrite
  //   COUNTER
  //   Select
  //   MUX
  //   INCRMNT
  //   Edge Flop
  //   Register
  //   D
  //   Clk
  //   Load
  //   Save
  //   Save Value
  //   Latch
  //   1 Bit mem
  //   SaveVal
  //   Always
  //   Loaded
  //   Reset
  //   Write
  //   Always OUT
  //   OUT
  //   Always On Out
  //   Out
endmodule

/* Test case:
C_2 C_1 C_0 A_0 B_0 O_0
0 0 1 9 6 15 #addition and subtraction
0 1 0 9 6 3
0 0 1 6 7 13
0 1 0 111 67 44
0 0 1 32 59 91
0 1 1 51 60 48  #and
0 1 1 3 2 2
0 1 1 5 3 1
0 1 1 12 25 8
0 1 1 4 8 0
1 0 1 5 3 7 #or
1 0 1 2 8 10
1 0 1 12 25 29
1 0 1 0 7 7
1 0 0 1 1 254 #nand
1 0 0 2 4 255
1 0 0 15 3 252
1 1 0 1 0 254 #nor
1 1 0 3 5 248
1 1 0 128 64 63
1 1 1 5 3 6 #xor
1 1 1 10 10 0
1 1 1 85 170 255
1 1 1 14 1 15
*/

/* Test case:
D C L ALWAYS LOADED
# 1. Randomized Startup: Register state is unknown (X). LOADED is 0 because L=0.
0x00 0 0 X 0x00

# 2. Load 0xAA: ALWAYS updates to 0xAA. LOADED shows it because L=1.
0xAA C 1 0xAA 0xAA

# 3. Transparent Check: ALWAYS stays 0xAA. LOADED drops to 0x00 because L=0.
0x55 0 0 0xAA 0x00
0x21 C 0 0x21 0x00

# 5. Load 0x00: Register becomes 0. Both pins show 0.
0x00 C 1 0x00 0x00

# 6. Edge-Triggering: Data 0xEE only moves to ALWAYS on the rising edge.
0xEE 0 1 0x00 0x00  # L=1, but no clock yet; LOADED is 0 because reg is 0
0xEE 1 1 0xEE 0xEE  # Clock goes high; Reg becomes 0xEE. LOADED now shows it.
0xDD 0 1 0xEE 0xEE  # Clock falls; Reg stays 0xEE.

# 7. High-Clock Stability Test
0xAA 0 1 0xEE 0xEE  # Prepare data 0xAA, but clock is 0. ALWAYS stays 0xEE.
0xAA 1 1 0xAA 0xAA  # Clock goes High. Register captures 0xAA.
0xFF 1 1 0xAA 0xAA  # DATA CHANGES TO 0xFF WHILE CLOCK IS STILL HIGH.
                    # ALWAYS MUST STAY 0xAA. If it changes to 0xFF, it's a latch!
*/
